# Fritzing sketch BioHackBoard (saved by Fritzing 0.9.2b)
stripboards: 1

parts:
  U3 = MMA_ACCEL_CONNECTOR [package=1x08]  # not connected
  Q3 = Basic FET P-Channel [package="TO220 [THT]"]
  Q4 = Basic FET P-Channel [package="TO220 [THT]"]
  J4 = male pin header, 3 pins [form="♂ (male)"]  # not connected
  J5 = male pin header, 2 pins [form="♂ (male)"]  # not connected
  J6 = male pin header, 2 pins [form="♂ (male)"]
  J8 = male pin header, 4 pins [form="♂ (male)"]
  J9 = male pin header, 4 pins [form="♂ (male)"]
  U4 = MMA_ACCEL_CONNECTOR [package=1x08]  # not connected
  J10 = Screw terminal - 2 pins [package=THT]  # not connected
  J11 = Screw terminal - 2 pins [package=THT]  # not connected
  J12 = male pin header, 3 pins [form="♂ (male)"]
  J13 = female pin header, 6 pins [form="♀ (female)"]
  U5 = MMA_ACCEL_CONNECTOR [package=1x08]  # not connected
  C1 = Electrolytic Capacitor [capacitance=100µF voltage=50V package="100 mil [THT, electrolytic]"]
  ULN1 = Darlington Driver [package=so018]  # not connected
  J15 = male pin header, 4 pins [form="♂ (male)"]  # not connected
  J16 = male pin header, 6 pins [form="♂ (male)"]
  J14 = male pin header, 2 pins [form="♂ (male)"]  # not connected
  J17 = male pin header, 2 pins [form="♂ (male)"]
  J18 = male pin header, 2 pins [form="♂ (male)"]  # not connected
  J19 = male pin header, 2 pins [form="♂ (male)"]  # not connected
  U6 = mystery part, 3 pins [chip_label=?]  # not connected
  U7 = mystery part, 3 pins [chip_label=?]

nets:
  N1: Q3.drain, J9.pin1, J13.pin6, J16.pin6, J17.pin1
  N2: Q4.drain, J6.pin2, J12.pin1, U7.pin2
  N3: J8.pin3, J9.pin3
  N4: C1.-, C1.+

notes:
  RENC2
  A  B  C
  I2C Connectors
  A0 A1 A2 A3 A4 A5
  Stepper
  Motor
  GND
  #13
  12
  #11
  #9
  #10
  8
  7
  #6
  #5
  4
  3
  1
  2
  0
  5V
  3V3
  VIN
  IOREFF
  RST
  V+ GND V+ GND
  Thermistor
  Connect
