# Fritzing sketch BioHackBoard (saved by Fritzing 0.9.3b)
stripboards: 1

parts:
  U3 = MMA_ACCEL_CONNECTOR [package=1x08]  # not connected
  Q3 = Basic FET P-Channel [package="TO220 [THT]"]  # not connected
  Q4 = Basic FET P-Channel [package="TO220 [THT]"]  # not connected
  J4 = male pin header, 3 pins [form="♂ (male)"]  # not connected
  J8 = male pin header, 4 pins [form="♂ (male)"]
  J9 = male pin header, 4 pins [form="♂ (male)"]
  U4 = MMA_ACCEL_CONNECTOR [package=1x08]  # not connected
  J10 = Screw terminal - 2 pins [package=THT]  # not connected
  J11 = Screw terminal - 2 pins [package=THT]  # not connected
  J13 = female pin header, 6 pins [form="♀ (female)"]  # not connected
  U5 = MMA_ACCEL_CONNECTOR [package=1x08]  # not connected
  C1 = Electrolytic Capacitor [capacitance=100µF voltage=50V package="100 mil [THT, electrolytic]"]
  ULN1 = Darlington Driver [package=so018]  # not connected
  J15 = male pin header, 4 pins [form="♂ (male)"]  # not connected
  J16 = male pin header, 6 pins [form="♂ (male)"]  # not connected
  J14 = male pin header, 2 pins [form="♂ (male)"]
  J17 = male pin header, 2 pins [form="♂ (male)"]  # not connected
  J18 = male pin header, 2 pins [form="♂ (male)"]  # not connected
  J19 = male pin header, 2 pins [form="♂ (male)"]  # not connected
  J20 = male pin header, 4 pins [form="♂ (male)"]
  J21 = male pin header, 2 pins [form="♂ (male)"]  # not connected
  J22 = male pin header, 2 pins [form="♂ (male)"]  # not connected

nets:
  N1: J8.pin3, J9.pin3
  N2: C1.-, C1.+
  N3: J14.pin2, J20.pin3

notes:
  I2C Connectors
  A0 A1 A2 A3 A4 A5
  Stepper Motor Connector
  GND
  #13
  12
  #11
  #9
  #10
  8
  7
  #6
  #5
  4
  3
  1
  2
  0
  5V
  3V3
  VIN
  IOREFF
  RST
  V+ GND V+ GND
  Thermistor
  Connect
  Rotary encoder
  A  B  C
