# Fritzing sketch Button Wiring (saved by Fritzing 0.9.3b)
breadboards: 1

parts:
  Arduino_Uno = Arduino Uno (Rev3)
  Push_Button = Pushbutton [package="[THT]"]
  R20 = Resistor [tolerance=±5% resistance=10k package=THT]

nets:
  N1: Arduino_Uno.D11_PWM/MOSI, Push_Button.Pin_3, Push_Button.Pin_4, R20.Pin_0
  N2: Arduino_Uno.5V, Push_Button.Pin_1, Push_Button.Pin_2
  N3: Arduino_Uno.GND, R20.Pin_1
