# Fritzing sketch Rotary Encoder Wiring (saved by Fritzing 0.9.3b)

parts:
  Arduino_Uno = Arduino Uno (Rev3)
  R1 = Rotary Potentiometer (Small) [maximum_resistance=100kΩ package=THT]

nets:
  N1: Arduino_Uno.D2, R1.leg2
  N2: Arduino_Uno.D3_PWM, R1.leg1
  N3: Arduino_Uno.GND, R1.wiper
